# Fritzing sketch PotentiometerDiagram (saved by Fritzing 0.9.3b)
breadboards: 1

parts:
  R1 = Resistor [tolerance=±5% resistance=220 package=THT]
  Part1 = Arduino Uno (Rev3)
  LED1 = smd LED [color="Red (633nm)" package="0805 [SMD]"]
  RE1 = Rotary Encoder [package=THT]

nets:
  N1: R1.Pin_0, LED1.anode
  N2: R1.Pin_1, Part1.5V, RE1.EncoderPinA
  N3: Part1.A0, RE1.EncoderPinC
  N4: Part1.D6_PWM, LED1.cathode
  N5: Part1.GND, RE1.EncoderPinB
